// Logisim project CPU.circ as structural Verilog: 4 circuits, main circuit main
module main (
);

  wire a_op, and_1_out, Branch, CLK, d_ff_1_q, Jump, MemRead, MemWrite, not_1_out, RegWrite, sel, ZF;
  wire [1:0] Reg_Addr, wm_sel;
  wire [3:0] opcode;
  wire [7:0] adder_1_out, alu_1_alu_out, Imm, multiplexer_1_out, PC_q, R3_pointer, r_op, Reg_Out, W_MUX;
  wire [9:8] rom_1_data;

  ROM #(.dataWidth(16)) rom_1 (.addr(PC_q), .data({opcode, Reg_Addr, rom_1_data, Imm}));
  Multiplexer #(.width(8)) multiplexer_1 (.in0(adder_1_out), .in1(Imm), .out(multiplexer_1_out), .sel(sel));
  Register PC (.D(multiplexer_1_out), .clk(CLK), .Q(PC_q));  // open: en, clr
  Adder adder_1 (.a(PC_q), .b(8'h1), .out(adder_1_out));  // open: cin, cout
  Clock clock_1 (.out(CLK));
  D_Flip_Flop d_ff_1 (.clk(CLK), .D(ZF), .Q(d_ff_1_q));  // open: Qn, preset, reset
  not not_1 (not_1_out, d_ff_1_q);
  and and_1 (and_1_out, not_1_out, Branch);
  Control_Unit control_unit_1 (
    .Opcode(opcode), .RegWrite(RegWrite), .Mem_Write(MemWrite), .Mem_Read(MemRead), .ALU_op(a_op),
    .DataReg(wm_sel[0]), .ImmReg(wm_sel[1]), .Branch(Branch), .Jump(Jump));
  Register_File register_file_1 (
    .RegWrite(RegWrite), .Write_Addr(Reg_Addr), .Data_In(W_MUX), .Clock(CLK), .Read_Addr(Reg_Addr),
    .R3_Pointer(R3_pointer), .Reg_Out(Reg_Out));
  ALU alu_1 (.In_A(Reg_Out), .ALU_op(a_op), .In_B(Imm), .ALU_Out(alu_1_alu_out), .Zero_Flag(ZF));
  or or_1 (sel, and_1_out, Jump);
  RAM #(.trigger("falling")) ram_1 (
    .addr(R3_pointer), .we(MemWrite), .oe(MemRead), .clk(CLK), .din(Reg_Out), .dout(r_op));
  // Probe on R3_pointer
  // Probe on r_op
  Multiplexer #(.select(2), .width(8)) multiplexer_2 (
    .in0(alu_1_alu_out), .in1(r_op), .in2(Imm), .out(W_MUX), .sel(wm_sel));  // open: in3

  // Notes on the sheet:
  //   contents of rom_1 (hex, n*v repeats v):
  //   c00 1400 800 3c01 1000 4c01 2000 3801 3c01 5809 6003 2400 7000
endmodule

module Control_Unit (
  input  [3:0] Opcode,
  output RegWrite,
  output Mem_Write,
  output Mem_Read,
  output ALU_op,
  output DataReg,
  output ImmReg,
  output Branch,
  output Jump
);

  ROM #(.addrWidth(4)) IR (
    .addr(Opcode), .data({Jump, Branch, ImmReg, DataReg, ALU_op, Mem_Read, Mem_Write, RegWrite}));

  // Notes on the sheet:
  //   contents of IR (hex, n*v repeats v):
  //   21 15 2 1 9 8 40 80
endmodule

module ALU (
  input  [7:0] In_A,
  input  ALU_op,
  input  [7:0] In_B,
  output [7:0] ALU_Out,
  output Zero_Flag
);

  wire [7:0] adder_1_out, subtractor_1_out;

  Adder adder_1 (.a(In_A), .b(In_B), .out(adder_1_out));  // open: cin, cout
  Subtractor subtractor_1 (.a(In_A), .b(In_B), .out(subtractor_1_out));  // open: bin, bout
  Multiplexer #(.width(8)) multiplexer_1 (.in0(adder_1_out), .in1(subtractor_1_out), .out(ALU_Out), .sel(ALU_op));
  nor nor_1 (Zero_Flag, subtractor_1_out[0], subtractor_1_out[1], subtractor_1_out[2], subtractor_1_out[3], subtractor_1_out[4], subtractor_1_out[5], subtractor_1_out[6], subtractor_1_out[7]);
endmodule

module Register_File (
  input  RegWrite,
  input  [1:0] Write_Addr,
  input  [7:0] Data_In,
  input  Clock,
  input  [1:0] Read_Addr,
  output [7:0] R3_Pointer,
  output [7:0] Reg_Out
);

  wire decoder_1_out0, decoder_1_out1, decoder_1_out2, decoder_1_out3;
  wire [7:0] R0_q, R1_q, R2_q;

  Decoder #(.select(2)) decoder_1 (
    .out0(decoder_1_out0), .out1(decoder_1_out1), .out2(decoder_1_out2), .out3(decoder_1_out3),
    .sel(Write_Addr), .en(RegWrite));
  Register R0 (.D(Data_In), .en(decoder_1_out0), .clk(Clock), .Q(R0_q));  // open: clr
  Multiplexer #(.select(2), .width(8)) multiplexer_1 (
    .in0(R0_q), .in1(R1_q), .in2(R2_q), .in3(R3_Pointer), .out(Reg_Out), .sel(Read_Addr));
  Register R1 (.D(Data_In), .en(decoder_1_out1), .clk(Clock), .Q(R1_q));  // open: clr
  Register R2 (.D(Data_In), .en(decoder_1_out2), .clk(Clock), .Q(R2_q));  // open: clr
  Register R3 (.D(Data_In), .en(decoder_1_out3), .clk(Clock), .Q(R3_Pointer));  // open: clr
endmodule
